# Fritzing sketch receiver (saved by Fritzing 0.9.10b)

parts:
  esp1 = ESP32 DevKitc V4
  Part2 = KY-022 Infrared Receiver Module [package="Breakout board"]

nets:
  3V3: esp1.3V3, Part2.Vin
  N1: esp1.GND, Part2.-
  N2: esp1.IO13, Part2.S

custom parts:
  ESP32 DevKitc V4: ESP32-DevKitC board with ESP32-WROOM-32 module. ESP32-DevKitC V4 is a small-sized ESP32-based development board produced by Espressif. Most of the pins on the ESP module are broken out to the pin headers on the board. The pins D0, D1, D2, D3, CMD and CLK are used internally for communication between ESP32 and SPI flash memory. They are grouped on both sides near the USB connector. Avoid using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
  KY-022 Infrared Receiver Module: Arduino IR receiver module KY-022, based on 1838 IR Receiver/Decoder. It reacts to 38kHz infrared light.
